# Fritzing sketch awt_fritzing (saved by Fritzing 0.9.2b)
perfboards: 1

parts:
  LT1763-3_3 = IC, DIP package, 8 pins
  C3 = Electrolytic Capacitor [capacitance=10µF package="100 mil [THT, electrolytic]"]
  C1 = Ceramic Capacitor [capacitance=1µF voltage=20V package="100 mil [THT, multilayer]"]
  BAT1 = Battery block 9V
  C2 = Capacitor [part_number=10nF package=cap-pth-small2]
  R1 = Resistor [tolerance=±5% resistance=220 package=THT]
  S1 = Toggle Switch [package=THT]
  U1 = attiny85 [package=dip]
  RHT1 = Humidity and Temperature Sensor RHT03
  U2 = RF-LINK_TX [package=rf-link_tx]
  R2 = Resistor [tolerance=±5% resistance=220 package=THT]
  LED1 = LED - 3mm [color="Red (633nm)" package="3 mm [THT]"]
  S2 = Pushbutton [package=THT]

nets:
  VCC: LT1763-3_3.pin1, LT1763-3_3.pin2, C3.+, C2.2, R1.Pin_0, U1.Pin_8, RHT1.Vcc, U2.+5V
  N1: LT1763-3_3.pin4, C2.1
  N2: LT1763-3_3.pin5, LT1763-3_3.pin8, S1.COM
  N3: LT1763-3_3.pin6, LT1763-3_3.pin7, C3.-, C1.0, BAT1.-, U1.Pin_4, RHT1.GND_1, RHT1.GND_2, U2.GND, R2.Pin_0, S2.leg1
  N4: C1.1, BAT1.+, S1.L1
  N5: R1.Pin_1, U1.Pin_5, RHT1.Data-signal
  N6: U1.Pin_1, S2.leg0
  N7: U1.Pin_3, LED1.anode
  N8: U1.Pin_6, U2.DATA
  N9: R2.Pin_1, LED1.cathode

notes:
  ON/OFF
  103
  10µF
  6.3v
  105
  LT
  1763
  DHT22
  RADIO
  antenna
